// Logisim project new_datapath.circ as structural Verilog: 7 circuits, main circuit main
module main (
  input  [1:0] P1,
  input  [1:0] P2,
  input  START,
  output [4:0] TO_PLAY,
  output [4:0] PLAYED,
  output ENDABLE,
  output W1,
  output W2,
  output D
);

  wire CLK_out, game_adv_1_draw, game_adv_1_w1, game_adv_1_w2, match_winner_1_invalid, match_winner_1_w1,
       match_winner_1_w2;
  wire [1:0] tmp_winner_1_pw_tmp;
  wire [4:0] game_adv_1_adv;

  tmp_winner tmp_winner_1 (.P1(P1), .P2(P2), .PW_TMP(tmp_winner_1_pw_tmp));
  match_winner match_winner_1 (
    .CLK(CLK_out), .P1(P1), .P2(P2), .PW_TMP(tmp_winner_1_pw_tmp), .START(START), .W1(match_winner_1_w1),
    .W2(match_winner_1_w2), .INVALID(match_winner_1_invalid));  // open: D
  Clock CLK (.out(CLK_out));
  set_total_manche set_total_manche_1 (.CLK(CLK_out), .START(START), .P1(P1), .P2(P2), .TO_PLAY(TO_PLAY));
  game_adv game_adv_1 (
    .CLK(CLK_out), .WIN1(match_winner_1_w1), .WIN2(match_winner_1_w2), .START(START), .W1(game_adv_1_w1),
    .W2(game_adv_1_w2), .DRAW(game_adv_1_draw), .ADV(game_adv_1_adv));
  game_count game_count_1 (.CLK(CLK_out), .START(START), .INVALID(match_winner_1_invalid), .PLAYED(PLAYED));
  end_game end_game_1 (
    .MATCH_ADV(game_adv_1_adv), .D(game_adv_1_draw), .W2(game_adv_1_w2), .W1(game_adv_1_w1), .PLAYED(PLAYED),
    .TO_PLAY(TO_PLAY), .WIN1(W1), .WIN2(W2), .DRAW(D), .ENDABLE(ENDABLE));
endmodule

module tmp_winner (
  input  [1:0] P1,
  input  [1:0] P2,
  output [1:0] PW_TMP
);

  wire and_1_out, and_2_out, and_3_out, and_4_out, comparator_1_eq, comparator_2_eq, comparator_3_eq,
       comparator_4_eq, comparator_5_eq, comparator_6_eq, comparator_7_eq, comparator_8_eq, comparator_9_eq,
       not_1_out, or_1_out, or_2_out;
  wire [1:0] multiplexer_1_out, multiplexer_2_out;

  Comparator #(.mode("unsigned"), .width(2)) comparator_1 (.a(P1), .b(2'b01), .eq(comparator_1_eq));  // open: gt, lt
  Comparator #(.mode("unsigned"), .width(2)) comparator_2 (.a(P2), .b(2'b11), .eq(comparator_2_eq));  // open: gt, lt
  and and_1 (and_1_out, comparator_1_eq, comparator_2_eq);
  Comparator #(.mode("unsigned"), .width(2)) comparator_3 (.a(P1), .b(2'b10), .eq(comparator_3_eq));  // open: gt, lt
  Comparator #(.mode("unsigned"), .width(2)) comparator_4 (.a(P2), .b(2'b01), .eq(comparator_4_eq));  // open: gt, lt
  and and_2 (and_2_out, comparator_3_eq, comparator_4_eq);
  or or_1 (or_1_out, and_1_out, and_2_out, and_3_out);
  Multiplexer #(.width(2)) multiplexer_1 (.in0(2'b10), .in1(2'b01), .out(multiplexer_1_out), .sel(or_1_out));
  Multiplexer #(.width(2)) multiplexer_2 (
    .in0(multiplexer_1_out), .in1(2'b00), .out(multiplexer_2_out), .sel(or_2_out));
  Comparator #(.mode("unsigned"), .width(2)) comparator_5 (.a(P1), .b(2'b11), .eq(comparator_5_eq));  // open: gt, lt
  Multiplexer #(.width(2)) multiplexer_3 (.in0(multiplexer_2_out), .in1(2'b11), .out(PW_TMP), .sel(and_4_out));
  Comparator #(.mode("unsigned"), .width(2)) comparator_6 (.a(P2), .b(2'b10), .eq(comparator_6_eq));  // open: gt, lt
  and and_3 (and_3_out, comparator_5_eq, comparator_6_eq);
  Comparator #(.mode("unsigned"), .width(2)) comparator_7 (.a(P1), .b(2'b00), .eq(comparator_7_eq));  // open: gt, lt
  or or_2 (or_2_out, comparator_7_eq, comparator_8_eq);
  Comparator #(.mode("unsigned"), .width(2)) comparator_8 (.a(P2), .b(2'b00), .eq(comparator_8_eq));  // open: gt, lt
  not not_1 (not_1_out, or_2_out);
  and and_4 (and_4_out, not_1_out, comparator_9_eq);
  Comparator #(.mode("unsigned"), .width(2)) comparator_9 (.a(P2), .b(P1), .eq(comparator_9_eq));  // open: gt, lt
endmodule

module set_total_manche (
  input  CLK,
  input  START,
  input  [1:0] P1,
  input  [1:0] P2,
  output [4:0] TO_PLAY
);

  wire adder_1_cout;
  wire [4:0] adder_1_out, adder_2_out, multiplexer_1_out, multiplexer_2_out, multiplexer_3_out;

  Multiplexer #(.select(2), .width(5)) multiplexer_1 (
    .in0({5{1'b0}}), .in1(5'b00100), .in2(5'b01000), .in3(5'b01100), .out(multiplexer_1_out), .sel(P1));
  Adder #(.width(5)) adder_1 (
    .a(multiplexer_2_out), .b(multiplexer_1_out), .out(adder_1_out), .cout(adder_1_cout));  // open: cin
  Multiplexer #(.select(2), .width(5)) multiplexer_2 (
    .in0({5{1'b0}}), .in1(5'b00001), .in2(5'b00010), .in3(5'b00011), .out(multiplexer_2_out), .sel(P2));
  Adder #(.width(5)) adder_2 (.a(adder_1_out), .b(5'b00100), .out(adder_2_out));  // open: cin, cout
  Multiplexer #(.width(5)) multiplexer_3 (.in0(TO_PLAY), .in1(adder_2_out), .out(multiplexer_3_out), .sel(START));
  Register #(.width(5)) FINAL (.D(multiplexer_3_out), .Q(TO_PLAY), .clk(CLK));  // open: en, clr
endmodule

module match_winner (
  input  CLK,
  input  [1:0] P1,
  input  [1:0] P2,
  input  [1:0] PW_TMP,
  input  START,
  output W1,
  output W2,
  output D,
  output INVALID
);

  wire comparator_1_eq, comparator_2_eq, comparator_3_eq, comparator_4_eq, comparator_5_eq, nor_1_out,
       or_1_out, WIN1_out, WIN2_out;
  wire [1:0] multiplexer_1_out, multiplexer_2_out, multiplexer_3_out, multiplexer_4_out, multiplexer_5_out,
       not_1_out, PREV_WM_q, PREV_WP_q;

  assign not_1_out = ~PREV_WM_q;  // NOT_Gate not_1, 2 bits wide
  Comparator #(.mode("unsigned"), .width(2)) comparator_1 (
    .a(PW_TMP), .b(2'b01), .eq(comparator_1_eq));  // open: gt, lt
  Comparator #(.mode("unsigned"), .width(2)) comparator_2 (
    .a(PW_TMP), .b(2'b10), .eq(comparator_2_eq));  // open: gt, lt
  Comparator #(.mode("unsigned"), .width(2)) comparator_3 (
    .a(PW_TMP), .b(2'b11), .eq(comparator_3_eq));  // open: gt, lt
  Comparator #(.mode("unsigned"), .width(2)) comparator_4 (
    .a(PW_TMP), .b(2'b00), .eq(comparator_4_eq));  // open: gt, lt
  Multiplexer #(.select(2), .width(2)) multiplexer_1 (
    .in0(PREV_WM_q), .in1(P1), .in2(P2), .in3(2'b00), .out(multiplexer_1_out), .sel(PW_TMP));
  Multiplexer #(.select(2), .width(2)) multiplexer_2 (
    .in0(not_1_out), .in1(P1), .in2(P2), .in3(not_1_out), .out(multiplexer_2_out), .sel(PREV_WP_q));
  Multiplexer #(.select(2), .width(2)) multiplexer_3 (
    .in0(PREV_WP_q), .in1(PW_TMP), .in2(PW_TMP), .in3(2'b00), .out(multiplexer_3_out), .sel(PREV_WP_q));
  nor nor_1 (nor_1_out, comparator_3_eq, comparator_4_eq);
  Multiplexer #(.width(2)) multiplexer_4 (.in0(multiplexer_1_out), .in1(2'b00), .out(multiplexer_4_out), .sel(START));
  Register #(.width(2)) PREV_WM (.D(multiplexer_4_out), .Q(PREV_WM_q), .clk(CLK));  // open: en, clr
  Multiplexer #(.width(2)) multiplexer_5 (.in0(multiplexer_3_out), .in1(2'b00), .out(multiplexer_5_out), .sel(START));
  Register #(.width(2)) PREV_WP (.D(multiplexer_5_out), .Q(PREV_WP_q), .clk(CLK));  // open: en, clr
  and WIN1 (WIN1_out, comparator_1_eq, nor_1_out);
  and WIN2 (WIN2_out, comparator_2_eq, nor_1_out);
  Comparator #(.mode("unsigned"), .width(2)) comparator_5 (
    .a(PREV_WM_q), .b(multiplexer_2_out), .eq(comparator_5_eq));  // open: gt, lt
  or or_1 (or_1_out, comparator_4_eq, comparator_5_eq);
  Multiplexer multiplexer_6 (.in0(WIN1_out), .in1(1'b0), .out(W1), .sel(START));
  Multiplexer multiplexer_7 (.in0(WIN2_out), .in1(1'b0), .out(W2), .sel(START));
  Multiplexer multiplexer_8 (.in0(comparator_3_eq), .in1(1'b0), .out(D), .sel(START));
  Multiplexer multiplexer_9 (.in0(or_1_out), .in1(1'b0), .out(INVALID), .sel(START));

  // Notes on the sheet:
  //   draw
  //   invalid
endmodule

module game_count (
  input  CLK,
  input  START,
  input  INVALID,
  output [4:0] PLAYED
);

  wire [4:0] adder_1_out, multiplexer_1_out, multiplexer_2_out;

  Adder #(.width(5)) adder_1 (.a(PLAYED), .b(5'b00001), .out(adder_1_out));  // open: cin, cout
  Multiplexer #(.width(5)) multiplexer_1 (.in0(adder_1_out), .in1(PLAYED), .out(multiplexer_1_out), .sel(INVALID));
  Multiplexer #(.width(5)) multiplexer_2 (
    .in0(multiplexer_1_out), .in1({5{1'b0}}), .out(multiplexer_2_out), .sel(START));
  Register #(.width(5)) PLAYED_M (.D(multiplexer_2_out), .Q(PLAYED), .clk(CLK));  // open: en, clr
endmodule

module game_adv (
  input  CLK,
  input  WIN1,
  input  WIN2,
  input  START,
  output W1,
  output W2,
  output DRAW,
  output [4:0] ADV
);

  wire [4:0] adder_1_out, adder_2_out, multiplexer_1_out, multiplexer_2_out, multiplexer_3_out,
       multiplexer_4_out, subtractor_1_out, subtractor_2_out, WCOUNT_1_q, WCOUNT_2_q;

  Adder #(.width(5)) adder_1 (.a(WCOUNT_1_q), .b(5'b00001), .out(adder_1_out));  // open: cin, cout
  Adder #(.width(5)) adder_2 (.a(WCOUNT_2_q), .b(5'b00001), .out(adder_2_out));  // open: cin, cout
  Multiplexer #(.width(5)) multiplexer_1 (.in0(WCOUNT_1_q), .in1(adder_1_out), .out(multiplexer_1_out), .sel(WIN1));
  Multiplexer #(.width(5)) multiplexer_2 (
    .in0(multiplexer_1_out), .in1({5{1'b0}}), .out(multiplexer_2_out), .sel(START));
  Multiplexer #(.width(5)) multiplexer_3 (.in0(WCOUNT_2_q), .in1(adder_2_out), .out(multiplexer_3_out), .sel(WIN2));
  Multiplexer #(.width(5)) multiplexer_4 (
    .in0(multiplexer_3_out), .in1({5{1'b0}}), .out(multiplexer_4_out), .sel(START));
  Register #(.width(5)) WCOUNT_1 (.D(multiplexer_2_out), .Q(WCOUNT_1_q), .clk(CLK));  // open: en, clr
  Register #(.width(5)) WCOUNT_2 (.D(multiplexer_4_out), .Q(WCOUNT_2_q), .clk(CLK));  // open: en, clr
  Comparator #(.mode("unsigned"), .width(5)) comparator_1 (.a(WCOUNT_1_q), .b(WCOUNT_1_q), .gt(W1));  // open: eq, lt
  Comparator #(.mode("unsigned"), .width(5)) comparator_2 (.a(WCOUNT_1_q), .b(WCOUNT_1_q), .eq(DRAW));  // open: gt, lt
  Subtractor #(.width(5)) subtractor_1 (.a(WCOUNT_1_q), .b(WCOUNT_2_q), .out(subtractor_1_out));  // open: bin, bout
  Subtractor #(.width(5)) subtractor_2 (.a(WCOUNT_2_q), .b(WCOUNT_1_q), .out(subtractor_2_out));  // open: bin, bout
  nor nor_1 (W2, W1, DRAW);
  Multiplexer #(.width(5)) multiplexer_5 (.in0(subtractor_1_out), .in1(subtractor_2_out), .out(ADV), .sel(DRAW));
endmodule

module end_game (
  input  [4:0] MATCH_ADV,
  input  D,
  input  W2,
  input  W1,
  input  [4:0] PLAYED,
  input  [4:0] TO_PLAY,
  output WIN1,
  output WIN2,
  output DRAW,
  output ENDABLE
);

  wire and_1_out, comparator_1_gt, comparator_2_eq, comparator_3_gt, or_1_out;

  Comparator #(.width(5)) comparator_1 (.a(PLAYED), .b(5'b00011), .gt(comparator_1_gt));  // open: eq, lt
  Comparator #(.width(5)) comparator_2 (.a(TO_PLAY), .b(PLAYED), .eq(comparator_2_eq));  // open: gt, lt
  or or_1 (or_1_out, comparator_1_gt, comparator_2_eq);
  Comparator #(.width(5)) comparator_3 (.a(MATCH_ADV), .b(5'b00001), .gt(comparator_3_gt));  // open: eq, lt
  and and_1 (and_1_out, comparator_3_gt, comparator_1_gt);
  or or_2 (ENDABLE, and_1_out, comparator_2_eq);
  and and_2 (WIN1, W1, or_1_out);
  and and_3 (WIN2, W2, or_1_out);
  and and_4 (DRAW, or_1_out, D);

  // Notes on the sheet:
  //   END GAME
endmodule
